// Logisim project jogo.circ as structural Verilog
module circuito_diferenca (
  input  [3:0] ESCOLHA_USUARIO_A,
  input  [3:0] ESCOLHA_CPU_B,
  output [3:0] DISTANCIA
);

  wire and_1_out, and_2_out, and_3_out, and_4_out, and_5_out, and_6_out, and_7_out, and_8_out, and_9_out,
       and_10_out, and_11_out, and_12_out, and_13_out, and_14_out, and_15_out, and_16_out, and_17_out,
       and_18_out, and_19_out, and_20_out, not_1_out, not_2_out, not_3_out, not_4_out, not_5_out, not_6_out,
       not_7_out, not_8_out, not_9_out, not_10_out, not_11_out, not_12_out, not_13_out, not_14_out,
       xor_1_out, xor_2_out, xor_3_out, xor_4_out, xor_5_out, xor_6_out, xor_10_out, xor_12_out, xor_14_out,
       xor_16_out, xor_18_out, xor_20_out;
  wire [3:0] xor_7_out, xor_8_out;

  not not_1 (not_1_out, ESCOLHA_USUARIO_A[0]);
  not not_2 (not_2_out, ESCOLHA_CPU_B[0]);
  xor xor_1 (xor_1_out, ESCOLHA_CPU_B[1], ESCOLHA_USUARIO_A[1]);
  and and_1 (and_1_out, and_19_out, ESCOLHA_CPU_B[1]);
  and and_2 (and_2_out, and_19_out, not_3_out);
  not not_3 (not_3_out, ESCOLHA_USUARIO_A[1]);
  not not_4 (not_4_out, ESCOLHA_USUARIO_A[1]);
  and and_3 (and_3_out, not_4_out, ESCOLHA_CPU_B[1]);
  xor xor_2 (xor_2_out, ESCOLHA_USUARIO_A[1], ESCOLHA_CPU_B[1]);
  and and_4 (and_4_out, and_20_out, ESCOLHA_USUARIO_A[1]);
  and and_5 (and_5_out, and_20_out, not_5_out);
  not not_5 (not_5_out, ESCOLHA_CPU_B[1]);
  not not_6 (not_6_out, ESCOLHA_CPU_B[1]);
  and and_6 (and_6_out, not_6_out, ESCOLHA_USUARIO_A[1]);
  xor xor_3 (xor_3_out, ESCOLHA_CPU_B[2], ESCOLHA_USUARIO_A[2]);
  and and_7 (and_7_out, xor_10_out, ESCOLHA_CPU_B[2]);
  and and_8 (and_8_out, xor_10_out, not_7_out);
  not not_7 (not_7_out, ESCOLHA_USUARIO_A[2]);
  not not_8 (not_8_out, ESCOLHA_USUARIO_A[2]);
  and and_9 (and_9_out, not_8_out, ESCOLHA_CPU_B[2]);
  xor xor_4 (xor_4_out, ESCOLHA_CPU_B[2], ESCOLHA_USUARIO_A[2]);
  and and_10 (and_10_out, xor_12_out, ESCOLHA_USUARIO_A[2]);
  and and_11 (and_11_out, xor_12_out, not_9_out);
  not not_9 (not_9_out, ESCOLHA_CPU_B[2]);
  not not_10 (not_10_out, ESCOLHA_CPU_B[2]);
  and and_12 (and_12_out, not_10_out, ESCOLHA_USUARIO_A[2]);
  xor xor_5 (xor_5_out, ESCOLHA_CPU_B[3], ESCOLHA_USUARIO_A[3]);
  and and_13 (and_13_out, xor_14_out, ESCOLHA_CPU_B[3]);
  and and_14 (and_14_out, xor_14_out, not_11_out);
  not not_11 (not_11_out, ESCOLHA_USUARIO_A[3]);
  not not_12 (not_12_out, ESCOLHA_USUARIO_A[3]);
  and and_15 (and_15_out, not_12_out, ESCOLHA_CPU_B[3]);
  xor xor_6 (xor_6_out, ESCOLHA_CPU_B[3], ESCOLHA_USUARIO_A[3]);
  and and_16 (and_16_out, xor_16_out, ESCOLHA_USUARIO_A[3]);
  and and_17 (and_17_out, xor_16_out, not_13_out);
  not not_13 (not_13_out, ESCOLHA_CPU_B[3]);
  not not_14 (not_14_out, ESCOLHA_CPU_B[3]);
  and and_18 (and_18_out, not_14_out, ESCOLHA_USUARIO_A[3]);
  xor xor_7 (xor_7_out[0], ESCOLHA_CPU_B[0], ESCOLHA_USUARIO_A[0]);
  and and_19 (and_19_out, not_1_out, ESCOLHA_CPU_B[0]);
  xor xor_8 (xor_8_out[0], ESCOLHA_CPU_B[0], ESCOLHA_USUARIO_A[0]);
  and and_20 (and_20_out, not_2_out, ESCOLHA_USUARIO_A[0]);
  xor xor_9 (xor_7_out[1], xor_1_out, and_19_out);
  ExactlyOne xor_10 (.out(xor_10_out), .in0(and_1_out), .in1(and_2_out), .in2(and_3_out));
  xor xor_11 (xor_8_out[1], xor_2_out, and_20_out);
  ExactlyOne xor_12 (.out(xor_12_out), .in0(and_4_out), .in1(and_5_out), .in2(and_6_out));
  xor xor_13 (xor_7_out[2], xor_3_out, xor_10_out);
  ExactlyOne xor_14 (.out(xor_14_out), .in0(and_7_out), .in1(and_8_out), .in2(and_9_out));
  xor xor_15 (xor_8_out[2], xor_4_out, xor_12_out);
  ExactlyOne xor_16 (.out(xor_16_out), .in0(and_10_out), .in1(and_11_out), .in2(and_12_out));
  xor xor_17 (xor_7_out[3], xor_5_out, xor_14_out);
  ExactlyOne xor_18 (.out(xor_18_out), .in0(and_13_out), .in1(and_14_out), .in2(and_15_out));
  xor xor_19 (xor_8_out[3], xor_6_out, xor_16_out);
  ExactlyOne xor_20 (.out(xor_20_out), .in0(and_16_out), .in1(and_17_out), .in2(and_18_out));
  Multiplexer #(.width(4)) multiplexer_1 (.in0(xor_7_out), .in1(xor_8_out), .out(DISTANCIA), .sel(xor_18_out));

  // Notes on the sheet:
  //   BIT 0 (B)
  //   BIT 0 (A)
  //   BIT 1 (B)
  //   BIT 1 (A)
  //   BIT 2 (B)
  //   BIT 2 (A)
  //   BIT 3 (B)
  //   BIT 3 (A)
  //   B.I. BIT 1 (A - B)
  //   B.I. BIT 1 (B - A)
  //   B.I. BIT 2 (A - B)
  //   B.I. BIT 2 (B - A)
  //   BIT 0 PARA (A - B)
  //   BIT 0 PARA (B - A)
  //   BIT 1 PARA (A - B)
  //   BIT 1 PARA (B-A)
  //   BIT 2 PARA (A - B)
  //   BIT 2 PARA (B-A)
  //   BIT 3 PARA (A - B)
  //   BIT 3 PARA (B-A)
  //   DESCOBRIR COMO FAZER GERAR UM NUMERO ALEATORIO DEPOIS QUE ACERTAR
  //   DIFF 0 (A - B)
  //   BOUT
  //   DIFF 0 (B - A)
  //   BOUT
  //   DIFF 1 (A - B)
  //   BOUT
  //   DIFF 1 (B - A)
  //   BOUT
  //   DIFF 2 (A - B)
  //   BOUT
  //   DIFF 2 (B - A)
  //   BOUT
  //   DIFF 3 (A - B)
  //   BOUT
  //   DIFF 3 (B - A)
  //   BOUT FINAL SEM USO (EM ANÁLISE)´
  //   Ditribuidor (A-B)
  //   Distribuidos (B - A)
endmodule
